# Fritzing sketch schematic (saved by Fritzing 0.8.7b)
breadboards: 1

parts:
  Part1 = Arduino Uno (Rev3)
  Part2 = 16 NeoPixel Ring [part_number=1463]
  Part4 = Adafruit MAX4466 Electret Microphone Amplifier [part_number="Adafruit #1063"]

nets:
  N1: Part1.A0, Part4.OUT
  N2: Part1.D10_PWM/SS, Part2.IN
  5V: Part1.5V, Part2.VDD, Part4.VCC
  GND: Part1.GND, Part2.GND, Part4.GND

custom parts:
  16 NeoPixel Ring: 16 ultra bright smart LED NeoPixels are arranged in a circle with 1.75" (44.5mm) outer diameter. The rings are 'chainable' - connect the output pin of one to the input pin of another. Use only one microcontroller pin to control as many as you can chain together! Each LED is addressable as the driver chip is inside the LED. Each one has ~18mA constant current drive so the color will be very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
  Adafruit MAX4466 Electret Microphone Amplifier: Add an ear to your project with this well-designed electret microphone amplifier. This fully assembled and tested board comes with a 20-20KHz electret microphone soldered on. For the amplification, we use the Maxim MAX4466, an op-amp specifically designed for this delicate task! The amplifier has excellent power supply noise rejection, so this amplifier sounds really good and isn't nearly as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
